# Fritzing sketch Density_based_Traffic_Control (saved by Fritzing 0.9.3b)
breadboards: 1

parts:
  Part1 = Arduino Mega 2560 (Rev3)
  M2 = fc-51 [package=THT]
  M3 = fc-51 [package=THT]
  M4 = fc-51 [package=THT]
  M5 = fc-51 [package=THT]
  M6 = fc-51 [package=THT]
  M7 = fc-51 [package=THT]
  M8 = fc-51 [package=THT]
  M9 = fc-51 [package=THT]
  LED2 = smd LED [color="Yellow (595nm)" package="0603 [SMD]"]
  LED3 = smd LED [color="Green (570nm)" package="0603 [SMD]"]
  LED4 = smd LED [color="Red (633nm)" package="0603 [SMD]"]
  SIDE_B = smd LED [color="Yellow (592nm)" package="0603 [SMD]"]
  LED6 = smd LED [color="Green (570nm)" package="0603 [SMD]"]
  LED7 = smd LED [color="Green (565nm)" package="0603 [SMD]"]
  SIDE_D = smd LED [color="Yellow (595nm)" package="0603 [SMD]"]
  LED9 = smd LED [color="Red (633nm)" package="0603 [SMD]"]
  LED10 = smd LED [color="Green (570nm)" package="0603 [SMD]"]
  LED11 = smd LED [color="Yellow (595nm)" package="0603 [SMD]"]
  SIDE_C = smd LED [color="Red (633nm)" package="0603 [SMD]"]
  R1 = Resistor [tolerance=±5% resistance=220 package=THT]
  R2 = Resistor [tolerance=±5% resistance=220 package="0402 [SMD]"]
  SIDE_A = smd LED [color="Red (633nm)" package="0603 [SMD]"]

nets:
  N1: Part1.D21/SCL, Part1.SCL, LED4.anode
  N2: Part1.D20/SDA, Part1.SDA, SIDE_B.anode
  N3: Part1.D19/RX1, LED6.anode
  N4: Part1.D16_PWM/TX2, SIDE_C.anode
  N5: Part1.D15/RX3, LED11.anode
  N6: Part1.D14/TX3, LED10.anode
  N7: Part1.GND, M2.pin2, M4.pin2, M7.pin2, R1.Pin_0, R2.Pin_1
  N8: Part1.D12_PWM, LED3.anode
  N9: Part1.D11_PWM, LED2.anode
  N10: Part1.D10_PWM, SIDE_A.anode
  N11: Part1.5V, M3.pin3, M4.pin3
  N12: Part1.D5_PWM, LED9.anode
  N13: Part1.D6_PWM, SIDE_D.anode
  N14: Part1.D7_PWM, LED7.anode
  N15: Part1.D23, M9.pin1
  N16: Part1.D25, M8.pin1
  N17: Part1.D31, M6.pin1
  N18: Part1.D33, M3.pin1
  N19: Part1.D43, M5.pin1
  N20: Part1.D45, M4.pin1
  N21: Part1.D51, M7.pin1
  N22: Part1.D53, M2.pin1
  N23: LED2.cathode, LED3.cathode, LED4.cathode, SIDE_B.cathode, LED6.cathode, R1.Pin_1, SIDE_A.cathode
  N24: LED7.cathode, SIDE_D.cathode, LED9.cathode, LED10.cathode, LED11.cathode, SIDE_C.cathode, R2.Pin_0

notes:
  S I D E A S I D E C
  S
  I
  D
  E
  B
  S
  I
  D
  E
  D
